# Fritzing sketch magspoof_schematic (saved by Fritzing 0.9.6b)
circuit board: 8.46667cm x 5.64444cm
breadboards: 1

parts:
  Arduino_Pro_Micro = Arduino Pro Micro (Clone)
  IC1 = L293D [package=THT]
  100uF_Capacitor = Capacitor Polarized [package=cpol-radial-100uf-25v]
  LED = smd LED [color="Red (633nm)" package="0603 [SMD]"]
  220_OHM_Resistor = Resistor [tolerance=±5% resistance=220 package="2010 [SMD]"]
  MAGNET_WIRE_COIL = Inductor [package="0603 [SMD]"]

nets:
  N1: Arduino_Pro_Micro.GND, IC1.0V, 220_OHM_Resistor.Pin_1
  N2: Arduino_Pro_Micro.D2, IC1.Enable_1, LED.anode
  N3: Arduino_Pro_Micro.D3, IC1.In_1
  N4: Arduino_Pro_Micro.D4, IC1.In_2
  N5: Arduino_Pro_Micro.VCC, IC1.+Vmotor, IC1.+V, 100uF_Capacitor.+, 100uF_Capacitor.-
  N6: IC1.Out_1_(_Controlled_by_Enable_1_), MAGNET_WIRE_COIL.pin_0
  N7: IC1.Out_2_(_Controlled_by_Enable_1_), MAGNET_WIRE_COIL.pin_1
  N8: LED.cathode, 220_OHM_Resistor.Pin_0
